# Fritzing sketch Hardware (saved by Fritzing 0.9.3b)

parts:
  Part1 = Arduino Uno (Rev3)
  Ultrasonic/Distance_Sensor = hc-sr04
  Relay = OMRON PCB Power Relay – G5LE [part_number="G5LE-1\n" package=THT]
  Solenoid_Valve/Pump_for_Alcohol = Solenoid

nets:
  N1: Part1.D8, Ultrasonic/Distance_Sensor.Trig
  N2: Part1.D2, Relay.COIL2
  N3: Part1.D7, Ultrasonic/Distance_Sensor.Echo
  5V: Part1.5V, Ultrasonic/Distance_Sensor.VCC
  N4: Part1.GND, Relay.COIL1, Relay.C
  N5: Part1.VIN, Solenoid_Valve/Pump_for_Alcohol.pin1
  N6: Relay.B, Solenoid_Valve/Pump_for_Alcohol.pin2
